# Fritzing sketch Untitled Sketch 4 (saved by Fritzing 0.9.3b)
breadboards: 2

parts:
  WeMos_D1_Mini1 = WeMos D1 Mini
  Часть1 = Gas Sensor Breakout Board
  J1 = Piezo Speaker
  RHT1 = Humidity and Temperature Sensor RHT03
  Lhi1 = LHi958 [package=to-39]

nets:
  5V: WeMos_D1_Mini1.5V, Часть1.B1, RHT1.Vcc, Lhi1.D
  N1: WeMos_D1_Mini1.A0, Часть1.A1
  N2: WeMos_D1_Mini1.D4, J1.pin2
  N3: WeMos_D1_Mini1.D5, RHT1.Data-signal
  GND: WeMos_D1_Mini1.G, Часть1.GND, J1.pin1, RHT1.GND_1, Lhi1.GND

// code stored in the sketch: Untitled4.ino
#include "DHT.h"
#define DHTPIN 2 // ??? ????? ????? ????, ? ??????? ??????????? ????
// ???? ?? ????????? ????? ???????????????. ??????? ???????????, ???? ??????????? ?????? DHT11 ? arduino
DHT dht(DHTPIN, DHT22); //????????? ???????
//DHT dht(DHTPIN, DHT11);
void setup() {
  Serial.begin(9600);
  dht.begin();
}
void loop() {
  delay(2000); // 2 ??????? ????????
  float h = dht.readHumidity(); //???????? ?????????
  float t = dht.readTemperature(); //???????? ???????????
  if (isnan(h) || isnan(t)) {  // ????????. ???? ?? ??????? ??????? ?????????, ????????? «?????? ??????????», ? ????????? ????????? ??????
    Serial.println("?????? ??????????");
    return;
  }
  Serial.print("?????????: ");
  Serial.print(h);
  Serial.print(" %\t");
  Serial.print("???????????: ");
  Serial.print(t);
  Serial.println(" *C "); //????? ??????????? ?? ?????
}
